# Fritzing sketch Innlevering2 (saved by Fritzing 0.9.2b)
circuit board: 8.46667cm x 5.64444cm
breadboards: 2

parts:
  TFT1 = 1.8" TFT Display with uSD
  J1 = Piezo Speaker
  RTC1 = DS1307 RTC Breakout
  IR1 = TSOP312.., 314.. [package=THT]
  U1 = ESP8266 WiFi Module [part_number=ESP8266]
  Part1 = Arduino Uno (Rev3) - ICSP
  R1 = Resistor [tolerance=±5% resistance=220 package="0805 [SMD]"]
  U2 = HC-SR04 [chip_label=IC package="SIP (Single Inline) [THT]"]

nets:
  N1: TFT1.SCK, Part1.D13/SCK
  N2: TFT1.MOSI, Part1.D11_PWM/MOSI
  N3: TFT1.CS, Part1.D9_PWM
  N4: TFT1.SDCS, Part1.D8
  N5: TFT1.D/C, Part1.D10_PWM/SS
  N6: TFT1.RST, Part1.D4
  N7: TFT1.VCC, Part1.D12/MISO
  N8: TFT1.GND, Part1.A0
  N9: J1.pin1, R1.Pin_0
  N10: J1.pin2, Part1.D3_PWM
  GND: RTC1.GND, IR1.Data, U1.GND, Part1.GND, R1.Pin_1, U2.GND
  5V: RTC1.5V, IR1.Vs, Part1.5V, U2.Vcc
  N11: RTC1.SDA, Part1.A5/SCL
  N12: RTC1.SCL, Part1.A4/SDA
  N13: IR1.GND, Part1.D0/RX
  N14: U1.RXD, Part1.D2
  VCC: U1.VCC, U1.CH_PD, Part1.3V3
  N15: U1.TXD, Part1.D7
  N16: Part1.A3, U2.Echo
  N17: Part1.D6_PWM, U2.Trig

custom parts:
  1.8" TFT Display with uSD: 1.8" TFT Display with SPI control and MicroSD card
  DS1307 RTC Breakout: DS1307 Real-time Clock Breakout Board with Battery
  ESP8266 WiFi Module: Generic WiFi Module based on the ESP8266 with onboard PCB antenna and UART communications
  HC-SR04: HC-SR04 ultrasound distance sensor
