# Fritzing sketch Innlevering1 (saved by Fritzing 0.9.2b)
circuit board: 8.46667cm x 5.64444cm
breadboards: 3

parts:
  Part1 = Arduino Uno (Rev3)
  U1 = 74HC595 [package="DIP16 [THT]"]
  U2 = MAX7219 [package=dil24]
  R1 = Resistor [tolerance=±5% resistance=220 package=THT]
  R2 = Resistor [tolerance=±5% resistance=220 package=THT]
  R3 = Resistor [tolerance=±5% resistance=220 package=THT]
  R4 = Resistor [tolerance=±5% resistance=220 package=THT]
  Disp1 = LBT2088AH [part_number=LBT2088AH]
  R5 = Resistor [tolerance=±5% resistance=10k package=THT]
  R6 = Resistor [tolerance=±5% resistance=220 package=THT]
  R7 = Resistor [tolerance=±5% resistance=220 package=THT]
  R8 = Resistor [tolerance=±5% resistance=220 package=THT]
  R9 = Resistor [tolerance=±5% resistance=220 package=THT]
  R10 = Resistor [tolerance=±5% resistance=330 package=THT]
  R11 = Resistor [tolerance=±5% resistance=330 package=THT]
  R12 = Resistor [tolerance=±5% resistance=330 package=THT]
  R13 = Resistor [tolerance=±5% resistance=330 package=THT]
  R14 = Resistor [tolerance=±5% resistance=330 package=THT]
  R15 = Resistor [tolerance=±5% resistance=330 package=THT]
  R16 = Resistor [tolerance=±5% resistance=330 package=THT]
  R17 = Resistor [tolerance=±5% resistance=330 package=THT]
  LCD1 = LCD screen  # not connected
  J1 = Piezo Speaker
  R18 = Resistor [tolerance=±5% resistance=330 package=THT]
  S1 = Pushbutton [package=THT]
  R19 = Resistor [tolerance=±5% resistance=10k package=THT]

nets:
  N1: Part1.D9_PWM, U2.LOAD
  N2: Part1.D10_PWM/SS, U1.DS
  N3: Part1.D11_PWM/MOSI, U1.ST_CP
  N4: Part1.D12/MISO, U1.SH_CP
  N5: Part1.D2, J1.pin2
  N6: Part1.D3_PWM, S1.leg0, R19.Pin_0
  N7: Part1.D5_PWM, U1.OE
  N8: Part1.D6_PWM, U1.MR
  N9: Part1.D7, U2.DIN
  5V: Part1.5V, U1.VCC, R5.Pin_0, S1.leg1
  GND: Part1.GND, U1.GND, U2.GND, U2.GND2, R18.Pin_1, R19.Pin_1
  N10: U1.Q1, R13.Pin_0
  N11: U1.Q2, R14.Pin_0
  N12: U1.Q3, R16.Pin_0
  N13: U1.Q4, R11.Pin_0
  N14: U1.Q5, R15.Pin_0
  N15: U1.Q6, R17.Pin_0
  N16: U1.Q7, R10.Pin_0
  N17: U1.Q0, R12.Pin_0
  N18: U2.DIG3, R6.Pin_0
  N19: U2.DIG7, R1.Pin_0
  N20: U2.DIG5, R3.Pin_0
  N21: U2.DIG1, R8.Pin_0
  N22: R2.Pin_1, Disp1.pin_8
  N23: R3.Pin_1, Disp1.pin_7
  N24: R4.Pin_1, Disp1.pin_6
  N25: Disp1.pin2, R9.Pin_1
  N26: Disp1.pin_3, R8.Pin_1
  N27: Disp1.pin_4, R7.Pin_1
  N28: Disp1.pin_5, R6.Pin_1
  N29: J1.pin1, R18.Pin_0
